// Logisim project 150116067_150117041_150117051.circ as structural Verilog: 17 circuits, main circuit registerfile
module main (
  input  in_1,
  output [3:0] out_2,
  output [17:0] out_3,
  output [9:0] out_4,
  output [17:0] out_5,
  output [4:0] out_6,
  output [13:0] out_7,
  output [13:0] out_8,
  output [17:0] out_9
);

  wire aluEnb, Bchooser, clk, CompEnb, Imm, MemLoad, not_1_out, pcEnb, pcSelect, RamEnb, readEnb, ready, ST,
       WE;
  wire [1:0] AluCho;
  wire [2:0] BChoise;
  wire [3:0] multiplexer_3_out, reg1, reg2;
  wire [5:0] _6bOut;
  wire [13:0] _14bOut, n6to14_1_p1;
  wire [17:0] controlled_buffer_2_out, INPUT, multiplexer_1_out, multiplexer_2_out, n6to18_1_out_2, OUTPUT,
       regout2, \ıns ;

  Clock clock_1 (.out(clk));
  PC pc_1 (
    .BInsBit(Bchooser), .BInsAddr(n6to14_1_p1), .OUT(out_8), .out_9(out_7), .JumpAddr(_14bOut),
    .PCselect(pcSelect), .ready(ready), .PCRead(pcEnb), .clk(clk), .reset(in_1));
  // _6to14 6to14_1: pin names not known; wires that end beside it: n6to14_1_p1, _6bOut
  Multiplexer #(.width(18), .enable("false")) multiplexer_1 (
    .in0(regout2), .in1(n6to18_1_out_2), .out(multiplexer_1_out), .sel(Imm));
  RAM #(.addrWidth(10), .dataWidth(18)) ram_1 (
    .addr(out_4), .data(out_3), .sel(RamEnb), .clk(clk), .ld(MemLoad), .clr(in_1));
  _6to18 u_6to18_1 (.in_1(_6bOut), .out_2(n6to18_1_out_2));
  ROM #(.addrWidth(14), .dataWidth(18)) rom_1 (.addr(out_8), .data(\ıns ));  // open: sel
  alu alu_1 (.IN1(out_5), .IN2(multiplexer_1_out), .ALUout(out_9), .in_3(AluCho), .AluEnable(aluEnb));
  Multiplexer #(.width(18), .enable("false")) multiplexer_2 (
    .in0(out_9), .out(multiplexer_2_out), .sel(MemLoad));  // open: in1
  Multiplexer #(.width(4), .enable("false")) multiplexer_3 (.in0(reg1), .in1(out_2), .out(multiplexer_3_out), .sel(ST));
  ControlUnit controlunit_1 (
    .ins(\ıns ), ._10bADD(out_4), .IMM_ADD(_6bOut), ._14bADD(_14bOut), .BChoise(BChoise), .Imm(Imm),
    .MEM_LOAD(MemLoad), .RamEnb(RamEnb), .DST(out_2), .REG1(reg1), .REG2(reg2), .WE(WE), .ALUEnb(aluEnb),
    .PCSelect(pcSelect), .PCEnable(pcEnb), .CompEnb(CompEnb), .readEnb(readEnb), .clr(in_1), .out_4(out_6),
    .ready(ready), .clk(clk), .ALUCho(AluCho), .out_19(ST));
  PCSelector pcselector_1 (.input1(out_5), .input2(regout2), .BChoise(BChoise), .Enable(CompEnb), .out(Bchooser));
  registerfile registerfile_1 (
    .RD1(multiplexer_3_out), .RD2(reg2), .WR(out_2), .WE(WE), .\input (multiplexer_2_out), .clk(clk),
    .reset(in_1), .OUT1(out_5), .OUT2(regout2));
  Register #(.width(18)) register_1 (.D(out_5), .en(ST), .Q(INPUT), .clk(clk), .clr(in_1));
  assign out_3 = not_1_out ? INPUT : 18'bz;  // Controlled_Buffer controlled_buffer_1
  not not_1 (not_1_out, MemLoad);
  assign controlled_buffer_2_out = MemLoad ? out_3 : 18'bz;  // Controlled_Buffer controlled_buffer_2
  Register #(.width(18)) register_2 (.D(controlled_buffer_2_out), .en(MemLoad), .Q(OUTPUT), .clk(clk), .clr(in_1));

  // Other names for the same wires on the sheet: _10bOut[9:0] = out_4; dst[3:0] = out_2; out[17:0] = out_9;
  //   RAMOut[17:0] = out_3; regout1[17:0] = out_5; rst = in_1

  // Notes on the sheet:
  //   spen 1 clock cycle for settign system
  //   Before starting the system we need to make rst 1 and 
  //   contents of rom_1 (hex, n*v repeats v):
  //   1844a 1844a 38400
endmodule

// Register File
module registerfile (
  input  [3:0] RD1,
  input  [3:0] RD2,
  input  [3:0] WR,
  input  WE,
  input  [17:0] \input ,
  input  clk,
  input  reset,
  output [17:0] OUT1,
  output [17:0] OUT2
);

  wire and_1_out, and_2_out, and_3_out, and_4_out, and_5_out, and_6_out, and_7_out, and_8_out, and_9_out,
       and_10_out, and_11_out, and_12_out, and_13_out, and_14_out, and_15_out, and_16_out, decoder_1_out0,
       decoder_1_out1, decoder_1_out2, decoder_1_out3, decoder_1_out4, decoder_1_out5, decoder_1_out6,
       decoder_1_out7, decoder_1_out8, decoder_1_out9, decoder_1_out10, decoder_1_out11, decoder_1_out12,
       decoder_1_out13, decoder_1_out14, decoder_1_out15, decoder_2_out0, decoder_2_out1, decoder_2_out2,
       decoder_2_out3, decoder_2_out4, decoder_2_out5, decoder_2_out6, decoder_2_out7, decoder_2_out8,
       decoder_2_out9, decoder_2_out10, decoder_2_out11, decoder_2_out12, decoder_2_out13, decoder_2_out14,
       decoder_2_out15, decoder_3_out0, decoder_3_out1, decoder_3_out2, decoder_3_out3, decoder_3_out4,
       decoder_3_out5, decoder_3_out6, decoder_3_out7, decoder_3_out8, decoder_3_out9, decoder_3_out10,
       decoder_3_out11, decoder_3_out12, decoder_3_out13, decoder_3_out14, decoder_3_out15;
  wire [17:0] register_1_q, register_2_q, register_3_q, register_4_q, register_5_q, register_6_q,
       register_7_q, register_8_q, register_9_q, register_10_q, register_11_q, register_12_q, register_13_q,
       register_14_q, register_15_q, register_16_q;

  Decoder #(.select(4), .enable("false")) decoder_1 (
    .out0(decoder_1_out0), .out1(decoder_1_out1), .out2(decoder_1_out2), .out3(decoder_1_out3),
    .out4(decoder_1_out4), .out5(decoder_1_out5), .out6(decoder_1_out6), .out7(decoder_1_out7),
    .out8(decoder_1_out8), .out9(decoder_1_out9), .out10(decoder_1_out10), .out11(decoder_1_out11),
    .out12(decoder_1_out12), .out13(decoder_1_out13), .out14(decoder_1_out14), .out15(decoder_1_out15),
    .sel(RD1));
  Decoder #(.select(4), .enable("false")) decoder_2 (
    .out0(decoder_2_out0), .out1(decoder_2_out1), .out2(decoder_2_out2), .out3(decoder_2_out3),
    .out4(decoder_2_out4), .out5(decoder_2_out5), .out6(decoder_2_out6), .out7(decoder_2_out7),
    .out8(decoder_2_out8), .out9(decoder_2_out9), .out10(decoder_2_out10), .out11(decoder_2_out11),
    .out12(decoder_2_out12), .out13(decoder_2_out13), .out14(decoder_2_out14), .out15(decoder_2_out15),
    .sel(RD2));
  Decoder #(.select(4), .enable("false")) decoder_3 (
    .out0(decoder_3_out0), .out1(decoder_3_out1), .out2(decoder_3_out2), .out3(decoder_3_out3),
    .out4(decoder_3_out4), .out5(decoder_3_out5), .out6(decoder_3_out6), .out7(decoder_3_out7),
    .out8(decoder_3_out8), .out9(decoder_3_out9), .out10(decoder_3_out10), .out11(decoder_3_out11),
    .out12(decoder_3_out12), .out13(decoder_3_out13), .out14(decoder_3_out14), .out15(decoder_3_out15),
    .sel(WR));
  and and_1 (and_1_out, decoder_3_out0, WE);
  and and_2 (and_2_out, decoder_3_out1, WE);
  and and_3 (and_3_out, decoder_3_out2, WE);
  and and_4 (and_4_out, decoder_3_out3, WE);
  and and_5 (and_5_out, decoder_3_out4, WE);
  and and_6 (and_6_out, decoder_3_out5, WE);
  and and_7 (and_7_out, decoder_3_out6, WE);
  and and_8 (and_8_out, decoder_3_out7, WE);
  and and_9 (and_9_out, decoder_3_out8, WE);
  and and_10 (and_10_out, decoder_3_out9, WE);
  and and_11 (and_11_out, decoder_3_out10, WE);
  and and_12 (and_12_out, decoder_3_out11, WE);
  and and_13 (and_13_out, decoder_3_out12, WE);
  and and_14 (and_14_out, decoder_3_out13, WE);
  and and_15 (and_15_out, decoder_3_out14, WE);
  and and_16 (and_16_out, decoder_3_out15, WE);
  Register #(.width(18)) register_1 (.D(\input ), .en(and_1_out), .Q(register_1_q), .clk(clk), .clr(reset));
  Register #(.width(18)) register_2 (.D(\input ), .en(and_2_out), .Q(register_2_q), .clk(clk), .clr(reset));
  Register #(.width(18)) register_3 (.D(\input ), .en(and_3_out), .Q(register_3_q), .clk(clk), .clr(reset));
  Register #(.width(18)) register_4 (.D(\input ), .en(and_4_out), .Q(register_4_q), .clk(clk), .clr(reset));
  Register #(.width(18)) register_5 (.D(\input ), .en(and_5_out), .Q(register_5_q), .clk(clk), .clr(reset));
  Register #(.width(18)) register_6 (.D(\input ), .en(and_6_out), .Q(register_6_q), .clk(clk), .clr(reset));
  Register #(.width(18)) register_7 (.D(\input ), .en(and_7_out), .Q(register_7_q), .clk(clk), .clr(reset));
  Register #(.width(18)) register_8 (.D(\input ), .en(and_8_out), .Q(register_8_q), .clk(clk), .clr(reset));
  Register #(.width(18)) register_9 (.D(\input ), .en(and_9_out), .Q(register_9_q), .clk(clk), .clr(reset));
  Register #(.width(18)) register_10 (.D(\input ), .en(and_10_out), .Q(register_10_q), .clk(clk), .clr(reset));
  Register #(.width(18)) register_11 (.D(\input ), .en(and_11_out), .Q(register_11_q), .clk(clk), .clr(reset));
  Register #(.width(18)) register_12 (.D(\input ), .en(and_12_out), .Q(register_12_q), .clk(clk), .clr(reset));
  Register #(.width(18)) register_13 (.D(\input ), .en(and_13_out), .Q(register_13_q), .clk(clk), .clr(reset));
  Register #(.width(18)) register_14 (.D(\input ), .en(and_14_out), .Q(register_14_q), .clk(clk), .clr(reset));
  Register #(.width(18)) register_15 (.D(\input ), .en(and_15_out), .Q(register_15_q), .clk(clk), .clr(reset));
  Register #(.width(18)) register_16 (.D(\input ), .en(and_16_out), .Q(register_16_q), .clk(clk), .clr(reset));
  assign OUT1 = decoder_1_out0 ? register_1_q : 18'bz;  // Controlled_Buffer controlled_buffer_1
  assign OUT2 = decoder_2_out0 ? register_1_q : 18'bz;  // Controlled_Buffer controlled_buffer_2
  assign OUT1 = decoder_1_out1 ? register_2_q : 18'bz;  // Controlled_Buffer controlled_buffer_3
  assign OUT2 = decoder_2_out1 ? register_2_q : 18'bz;  // Controlled_Buffer controlled_buffer_4
  assign OUT1 = decoder_1_out2 ? register_3_q : 18'bz;  // Controlled_Buffer controlled_buffer_5
  assign OUT2 = decoder_2_out2 ? register_3_q : 18'bz;  // Controlled_Buffer controlled_buffer_6
  assign OUT1 = decoder_1_out3 ? register_4_q : 18'bz;  // Controlled_Buffer controlled_buffer_7
  assign OUT2 = decoder_2_out3 ? register_4_q : 18'bz;  // Controlled_Buffer controlled_buffer_8
  assign OUT1 = decoder_1_out4 ? register_5_q : 18'bz;  // Controlled_Buffer controlled_buffer_9
  assign OUT2 = decoder_2_out4 ? register_5_q : 18'bz;  // Controlled_Buffer controlled_buffer_10
  assign OUT1 = decoder_1_out5 ? register_6_q : 18'bz;  // Controlled_Buffer controlled_buffer_11
  assign OUT2 = decoder_2_out5 ? register_6_q : 18'bz;  // Controlled_Buffer controlled_buffer_12
  assign OUT1 = decoder_1_out6 ? register_7_q : 18'bz;  // Controlled_Buffer controlled_buffer_13
  assign OUT2 = decoder_2_out6 ? register_7_q : 18'bz;  // Controlled_Buffer controlled_buffer_14
  assign OUT1 = decoder_1_out7 ? register_8_q : 18'bz;  // Controlled_Buffer controlled_buffer_15
  Controlled_Buffer #(.width(18)) controlled_buffer_16 (.out(OUT2), .en(decoder_2_out7));  // open: in
  assign OUT1 = decoder_1_out8 ? register_9_q : 18'bz;  // Controlled_Buffer controlled_buffer_17
  assign OUT2 = decoder_2_out8 ? register_9_q : 18'bz;  // Controlled_Buffer controlled_buffer_18
  assign OUT1 = decoder_1_out9 ? register_10_q : 18'bz;  // Controlled_Buffer controlled_buffer_19
  assign OUT2 = decoder_2_out9 ? register_10_q : 18'bz;  // Controlled_Buffer controlled_buffer_20
  assign OUT1 = decoder_1_out10 ? register_11_q : 18'bz;  // Controlled_Buffer controlled_buffer_21
  assign OUT2 = decoder_2_out10 ? register_11_q : 18'bz;  // Controlled_Buffer controlled_buffer_22
  assign OUT1 = decoder_1_out11 ? register_12_q : 18'bz;  // Controlled_Buffer controlled_buffer_23
  assign OUT2 = decoder_2_out11 ? register_12_q : 18'bz;  // Controlled_Buffer controlled_buffer_24
  assign OUT1 = decoder_1_out12 ? register_13_q : 18'bz;  // Controlled_Buffer controlled_buffer_25
  assign OUT2 = decoder_2_out12 ? register_13_q : 18'bz;  // Controlled_Buffer controlled_buffer_26
  assign OUT1 = decoder_1_out13 ? register_14_q : 18'bz;  // Controlled_Buffer controlled_buffer_27
  assign OUT2 = decoder_2_out13 ? register_14_q : 18'bz;  // Controlled_Buffer controlled_buffer_28
  assign OUT1 = decoder_1_out14 ? register_15_q : 18'bz;  // Controlled_Buffer controlled_buffer_29
  assign OUT2 = decoder_2_out14 ? register_15_q : 18'bz;  // Controlled_Buffer controlled_buffer_30
  assign OUT1 = decoder_1_out15 ? register_16_q : 18'bz;  // Controlled_Buffer controlled_buffer_31
  assign OUT2 = decoder_2_out15 ? register_16_q : 18'bz;  // Controlled_Buffer controlled_buffer_32
endmodule

// ALU
module alu (
  input  [17:0] IN1,
  input  [17:0] IN2,
  input  [1:0] in_3,
  input  AluEnable,
  output [17:0] ALUout
);

  wire [17:0] ADD, AND, OR, XOR;

  _18bAdder u_18badder_1 (.input2(IN2), .input1(IN1), .sum(ADD));  // open: co
  assign AND = IN1 & IN2;  // AND_Gate and_1, 18 bits wide
  assign OR = IN1 | IN2;  // OR_Gate or_1, 18 bits wide
  assign XOR = IN1 ^ IN2;  // XOR_Gate xor_1, 18 bits wide
  Multiplexer #(.select(2), .width(18)) multiplexer_1 (
    .in0(AND), .in1(OR), .in2(ADD), .in3(XOR), .out(ALUout), .sel(in_3), .en(AluEnable));
endmodule

module PC (
  input  [13:0] BInsAddr,
  input  BInsBit,
  input  reset,
  input  PCselect,
  input  [13:0] JumpAddr,
  input  ready,
  input  clk,
  input  PCRead,
  output [13:0] out_9,
  output [13:0] OUT
);

  wire [13:0] multiplexer_1_out, multiplexer_2_out, n14badder_1_sum;

  Multiplexer #(.width(14), .enable("false")) multiplexer_1 (
    .in0(14'h1), .in1(BInsAddr), .out(multiplexer_1_out), .sel(BInsBit));
  _14bAdder u_14badder_1 (.input2(multiplexer_1_out), .input1(out_9), .sum(n14badder_1_sum));  // open: co
  Multiplexer #(.width(14), .enable("false")) multiplexer_2 (
    .in0(n14badder_1_sum), .in1(JumpAddr), .out(multiplexer_2_out), .sel(PCselect));
  Register #(.width(14)) register_1 (.D(multiplexer_2_out), .en(ready), .Q(out_9), .clk(clk), .clr(reset));
  Register #(.width(14)) register_2 (.D(out_9), .en(PCRead), .Q(OUT), .clk(clk), .clr(reset));
endmodule

// CONTROL UNIT
module ControlUnit (
  input  clr,
  input  [17:0] ins,
  input  clk,
  output [4:0] out_4,
  output [9:0] _10bADD,
  output [1:0] ALUCho,
  output [5:0] IMM_ADD,
  output Imm,
  output [13:0] _14bADD,
  output MEM_LOAD,
  output RamEnb,
  output [3:0] DST,
  output [3:0] REG1,
  output [3:0] REG2,
  output WE,
  output [2:0] BChoise,
  output ALUEnb,
  output PCSelect,
  output out_19,
  output PCEnable,
  output CompEnb,
  output readEnb,
  output ready
);

  wire _6bEnb, _10bEnb, ADD, ADDI, AND, ANDI, BEQ, BGE, BGT, BLE, BLT, Fetch2, LD2, OR, ORI, ST2, XOR, XORI;

  assign _10bADD = _10bEnb ? ins[9:0] : 10'bz;  // Controlled_Buffer controlled_buffer_1
  assign IMM_ADD = _6bEnb ? ins[5:0] : 6'bz;  // Controlled_Buffer controlled_buffer_2
  assign _14bADD = PCSelect ? ins[13:0] : 14'bz;  // Controlled_Buffer controlled_buffer_3
  nor nor_1 (ready, PCEnable, Fetch2, MEM_LOAD);
  decoder_input decoder_input_1 (
    .ld1(MEM_LOAD), .in_5(ins[17:14]), .fetch1(PCEnable), .st1(out_19), .clr(clr), .clk(clk),
    .fetch2(Fetch2), .out_8(out_4));
  or or_1 (ALUEnb, OR, XOR, ORI, XORI, ADD, XOR, ADDI, XORI);
  Decoder #(.select(5), .enable("false")) decoder_1 (
    .out0(AND), .out1(OR), .out2(ADD), .out3(XOR), .out4(ANDI), .out5(ORI), .out6(ADDI), .out7(XORI),
    .out8(BEQ), .out9(BGT), .out10(BLT), .out11(BGE), .out12(BLE), .out13(MEM_LOAD), .out14(out_19),
    .out15(PCSelect), .out16(PCEnable), .out17(Fetch2), .out18(LD2), .out19(ST2), .sel(out_4));  // open: out20, out21, out22, out23, out24, out25, out26, out27, out28, out29, out30, out31
  or or_2 (_6bEnb, ANDI, ORI, XORI, ADDI, BEQ, BGT, BLT, BGE, BLE);
  or or_3 (CompEnb, BEQ, BGT, BLT, BGE, BLE);
  or or_4 (_10bEnb, ST2, MEM_LOAD);
  or or_5 (RamEnb, ST2, MEM_LOAD);
  nor nor_2 (readEnb, PCSelect, LD2, Fetch2, PCEnable, MEM_LOAD);
  or or_6 (ALUCho[0], OR, XOR, ORI, XORI);
  or or_7 (ALUCho[1], ADD, XOR, ADDI, XORI);
  or or_8 (Imm, ANDI, ORI, ADDI, XORI);
  or or_9 (WE, OR, XOR, ORI, XORI, LD2, ADD, XOR, ADDI, XORI);

  assign BChoise = ins[16:14];
  assign DST = ins[13:10];
  assign REG1 = ins[9:6];
  assign REG2 = ins[5:2];

  // Other names for the same wires on the sheet: Opcode[3:0] = ins[17:14]; Fetch1 = PCEnable; JUMP = PCSelect;
  //   LD = MEM_LOAD; ST = out_19
endmodule

// HA
module halfAdder (
  input  a,
  input  b,
  output sum,
  output co
);

  xor xor_1 (sum, b, a);
  and and_1 (co, b, a);
endmodule

// FA
module fullAdder (
  input  a,
  input  b,
  input  ci,
  output sum,
  output co
);

  wire and_1_out, and_2_out, and_3_out, or_1_out, xor_1_out;

  and and_1 (and_1_out, ~ci, b, a);  // AND_Gate
  or or_1 (or_1_out, b, a);
  ExactlyOne xor_1 (.out(xor_1_out), .in0(ci), .in1(b), .in2(a));
  and and_2 (and_2_out, or_1_out, ci);
  and and_3 (and_3_out, ci, b, a);
  or or_2 (co, and_1_out, and_2_out);
  or or_3 (sum, xor_1_out, and_3_out);
endmodule

module _18bAdder (
  input  [17:0] input2,
  input  [17:0] input1,
  output [17:0] sum,
  output co
);

  wire fulladder_1_co, fulladder_2_co, fulladder_3_co, fulladder_4_co, fulladder_5_co, fulladder_6_co,
       fulladder_7_co, fulladder_8_co, fulladder_9_co, fulladder_10_co, fulladder_11_co, fulladder_12_co,
       fulladder_13_co, fulladder_14_co, fulladder_15_co, fulladder_16_co, halfadder_1_co;

  halfAdder halfadder_1 (.a(input2[0]), .b(input1[0]), .sum(sum[0]), .co(halfadder_1_co));
  fullAdder fulladder_1 (.a(input2[1]), .b(input1[1]), .ci(halfadder_1_co), .sum(sum[1]), .co(fulladder_1_co));
  fullAdder fulladder_2 (.a(input2[2]), .b(input1[2]), .ci(fulladder_1_co), .sum(sum[2]), .co(fulladder_2_co));
  fullAdder fulladder_3 (.a(input2[3]), .b(input1[3]), .ci(fulladder_2_co), .sum(sum[3]), .co(fulladder_3_co));
  fullAdder fulladder_4 (.a(input2[4]), .b(input1[4]), .ci(fulladder_3_co), .sum(sum[4]), .co(fulladder_4_co));
  fullAdder fulladder_5 (.a(input2[5]), .b(input1[5]), .ci(fulladder_4_co), .sum(sum[5]), .co(fulladder_5_co));
  fullAdder fulladder_6 (.a(input2[6]), .b(input1[6]), .ci(fulladder_5_co), .sum(sum[6]), .co(fulladder_6_co));
  fullAdder fulladder_7 (.a(input2[7]), .b(input1[7]), .ci(fulladder_6_co), .sum(sum[7]), .co(fulladder_7_co));
  fullAdder fulladder_8 (.a(input2[8]), .b(input1[8]), .ci(fulladder_7_co), .sum(sum[8]), .co(fulladder_8_co));
  fullAdder fulladder_9 (.a(input2[9]), .b(input1[9]), .ci(fulladder_8_co), .sum(sum[9]), .co(fulladder_9_co));
  fullAdder fulladder_10 (.a(input2[10]), .b(input1[10]), .ci(fulladder_9_co), .sum(sum[10]), .co(fulladder_10_co));
  fullAdder fulladder_11 (.a(input2[11]), .b(input1[11]), .ci(fulladder_10_co), .sum(sum[11]), .co(fulladder_11_co));
  fullAdder fulladder_12 (.a(input2[12]), .b(input1[12]), .ci(fulladder_11_co), .sum(sum[12]), .co(fulladder_12_co));
  fullAdder fulladder_13 (.a(input2[13]), .b(input1[13]), .ci(fulladder_12_co), .sum(sum[13]), .co(fulladder_13_co));
  fullAdder fulladder_14 (.a(input2[14]), .b(input1[14]), .ci(fulladder_13_co), .sum(sum[14]), .co(fulladder_14_co));
  fullAdder fulladder_15 (.a(input2[15]), .b(input1[15]), .ci(fulladder_14_co), .sum(sum[15]), .co(fulladder_15_co));
  fullAdder fulladder_16 (.a(input2[16]), .b(input1[16]), .ci(fulladder_15_co), .sum(sum[16]), .co(fulladder_16_co));
  fullAdder fulladder_17 (.a(input2[17]), .b(input1[17]), .ci(fulladder_16_co), .sum(sum[17]), .co(co));
endmodule

// HC
module HalfComp (
  input  a,
  input  b,
  output G,
  output E,
  output L
);

  and and_1 (G, ~b, a);  // AND_Gate
  xnor xnor_1 (E, b, a);
  and and_2 (L, b, ~a);  // AND_Gate
endmodule

// FC
module FullComp (
  input  L_in,
  input  E_in,
  input  G_in,
  input  a,
  input  b,
  output L,
  output E,
  output G
);

  wire and_1_out, and_2_out, xnor_1_out;

  and and_1 (and_1_out, ~b, a, E_in);  // AND_Gate
  xnor xnor_1 (xnor_1_out, b, a);
  and and_2 (and_2_out, b, ~a, G_in);  // AND_Gate
  or or_1 (G, and_1_out, G_in);
  and and_3 (E, xnor_1_out, G_in);
  or or_2 (L, and_2_out, L_in);
endmodule

module _18bComp (
  input  [17:0] input1,
  input  [17:0] input2,
  output ZF,
  output PF,
  output NF
);

  wire fullcomp_1_e, fullcomp_1_g, fullcomp_1_l, fullcomp_2_e, fullcomp_2_g, fullcomp_2_l, fullcomp_3_e,
       fullcomp_3_g, fullcomp_3_l, fullcomp_4_e, fullcomp_4_g, fullcomp_4_l, fullcomp_5_e, fullcomp_5_g,
       fullcomp_5_l, fullcomp_6_e, fullcomp_6_g, fullcomp_6_l, fullcomp_7_e, fullcomp_7_g, fullcomp_7_l,
       fullcomp_8_e, fullcomp_8_g, fullcomp_8_l, fullcomp_9_e, fullcomp_9_g, fullcomp_9_l, fullcomp_10_e,
       fullcomp_10_g, fullcomp_10_l, fullcomp_11_e, fullcomp_11_g, fullcomp_11_l, fullcomp_12_e,
       fullcomp_12_g, fullcomp_12_l, fullcomp_13_e, fullcomp_13_g, fullcomp_13_l, fullcomp_14_e,
       fullcomp_14_g, fullcomp_14_l, fullcomp_15_e, fullcomp_15_g, fullcomp_15_l, fullcomp_16_e,
       fullcomp_16_g, fullcomp_16_l, fullcomp_17_e, fullcomp_17_g, fullcomp_17_l, halfcomp_1_e, halfcomp_1_g,
       halfcomp_1_l;

  HalfComp halfcomp_1 (.a(input1[0]), .b(input2[0]), .G(halfcomp_1_g), .E(halfcomp_1_e), .L(halfcomp_1_l));
  FullComp fullcomp_1 (
    .L_in(halfcomp_1_g), .E_in(halfcomp_1_e), .G_in(halfcomp_1_l), .b(input2[1]), .a(input1[1]),
    .L(fullcomp_1_l), .E(fullcomp_1_e), .G(fullcomp_1_g));
  FullComp fullcomp_2 (
    .L_in(fullcomp_1_l), .E_in(fullcomp_1_e), .G_in(fullcomp_1_g), .b(input2[2]), .a(input1[2]),
    .L(fullcomp_2_l), .E(fullcomp_2_e), .G(fullcomp_2_g));
  FullComp fullcomp_3 (
    .L_in(fullcomp_2_l), .E_in(fullcomp_2_e), .G_in(fullcomp_2_g), .b(input2[3]), .a(input1[3]),
    .L(fullcomp_3_l), .E(fullcomp_3_e), .G(fullcomp_3_g));
  FullComp fullcomp_4 (
    .L_in(fullcomp_3_l), .E_in(fullcomp_3_e), .G_in(fullcomp_3_g), .b(input2[4]), .a(input1[4]),
    .L(fullcomp_4_l), .E(fullcomp_4_e), .G(fullcomp_4_g));
  FullComp fullcomp_5 (
    .L_in(fullcomp_4_l), .E_in(fullcomp_4_e), .G_in(fullcomp_4_g), .b(input2[5]), .a(input1[5]),
    .L(fullcomp_5_l), .E(fullcomp_5_e), .G(fullcomp_5_g));
  FullComp fullcomp_6 (
    .L_in(fullcomp_5_l), .E_in(fullcomp_5_e), .G_in(fullcomp_5_g), .b(input2[6]), .a(input1[6]),
    .L(fullcomp_6_l), .E(fullcomp_6_e), .G(fullcomp_6_g));
  FullComp fullcomp_7 (
    .L_in(fullcomp_6_l), .E_in(fullcomp_6_e), .G_in(fullcomp_6_g), .b(input2[7]), .a(input1[7]),
    .L(fullcomp_7_l), .E(fullcomp_7_e), .G(fullcomp_7_g));
  FullComp fullcomp_8 (
    .L_in(fullcomp_7_l), .E_in(fullcomp_7_e), .G_in(fullcomp_7_g), .b(input2[8]), .a(input1[8]),
    .L(fullcomp_8_l), .E(fullcomp_8_e), .G(fullcomp_8_g));
  FullComp fullcomp_9 (
    .L_in(fullcomp_8_l), .E_in(fullcomp_8_e), .G_in(fullcomp_8_g), .b(input2[9]), .a(input1[9]),
    .L(fullcomp_9_l), .E(fullcomp_9_e), .G(fullcomp_9_g));
  FullComp fullcomp_10 (
    .L_in(fullcomp_9_l), .E_in(fullcomp_9_e), .G_in(fullcomp_9_g), .b(input2[10]), .a(input1[10]),
    .L(fullcomp_10_l), .E(fullcomp_10_e), .G(fullcomp_10_g));
  FullComp fullcomp_11 (
    .L_in(fullcomp_10_l), .E_in(fullcomp_10_e), .G_in(fullcomp_10_g), .b(input2[11]), .a(input1[11]),
    .L(fullcomp_11_l), .E(fullcomp_11_e), .G(fullcomp_11_g));
  FullComp fullcomp_12 (
    .L_in(fullcomp_11_l), .E_in(fullcomp_11_e), .G_in(fullcomp_11_g), .b(input2[12]), .a(input1[12]),
    .L(fullcomp_12_l), .E(fullcomp_12_e), .G(fullcomp_12_g));
  FullComp fullcomp_13 (
    .L_in(fullcomp_12_l), .E_in(fullcomp_12_e), .G_in(fullcomp_12_g), .b(input2[13]), .a(input1[13]),
    .L(fullcomp_13_l), .E(fullcomp_13_e), .G(fullcomp_13_g));
  FullComp fullcomp_14 (
    .L_in(fullcomp_13_l), .E_in(fullcomp_13_e), .G_in(fullcomp_13_g), .b(input2[14]), .a(input1[14]),
    .L(fullcomp_14_l), .E(fullcomp_14_e), .G(fullcomp_14_g));
  FullComp fullcomp_15 (
    .L_in(fullcomp_14_l), .E_in(fullcomp_14_e), .G_in(fullcomp_14_g), .b(input2[15]), .a(input1[15]),
    .L(fullcomp_15_l), .E(fullcomp_15_e), .G(fullcomp_15_g));
  FullComp fullcomp_16 (
    .L_in(fullcomp_15_l), .E_in(fullcomp_15_e), .G_in(fullcomp_15_g), .b(input2[16]), .a(input1[16]),
    .L(fullcomp_16_l), .E(fullcomp_16_e), .G(fullcomp_16_g));
  FullComp fullcomp_17 (
    .L_in(fullcomp_16_l), .E_in(fullcomp_16_e), .G_in(fullcomp_16_g), .b(input2[17]), .a(input1[17]),
    .L(fullcomp_17_l), .E(fullcomp_17_e), .G(fullcomp_17_g));
  and and_1 (ZF, ~fullcomp_17_l, fullcomp_17_e, ~fullcomp_17_g);  // AND_Gate
  and and_2 (PF, ~fullcomp_17_l, ~fullcomp_17_e, fullcomp_17_g);  // AND_Gate
  and and_3 (NF, fullcomp_17_l, ~fullcomp_17_e, ~fullcomp_17_g);  // AND_Gate
endmodule

module decoder_input (
  input  st1,
  input  clr,
  input  ld1,
  input  fetch2,
  input  [3:0] in_5,
  input  fetch1,
  input  clk,
  output [4:0] out_8
);

  wire nor_1_out, not_1_out;
  wire [4:0] controlled_buffer_1_out, controlled_buffer_6_out;

  assign controlled_buffer_1_out = nor_1_out ? 5'b10000 : 5'bz;  // Controlled_Buffer controlled_buffer_1
  nor nor_1 (nor_1_out, fetch1, fetch2, st1, ld1);
  assign controlled_buffer_1_out = st1 ? 5'b10011 : 5'bz;  // Controlled_Buffer controlled_buffer_2
  assign controlled_buffer_1_out = ld1 ? 5'b10010 : 5'bz;  // Controlled_Buffer controlled_buffer_3
  assign controlled_buffer_1_out = fetch2 ? {1'b0, in_5} : 5'bz;  // Controlled_Buffer controlled_buffer_4
  assign controlled_buffer_1_out = fetch1 ? 5'b10001 : 5'bz;  // Controlled_Buffer controlled_buffer_5
  assign controlled_buffer_6_out = clr ? 5'b10000 : 5'bz;  // Controlled_Buffer controlled_buffer_6
  not not_1 (not_1_out, clr);
  assign controlled_buffer_6_out = not_1_out ? controlled_buffer_1_out : 5'bz;  // Controlled_Buffer controlled_buffer_7
  Register #(.width(5)) register_1 (.D(controlled_buffer_6_out), .Q(out_8), .clk(clk));  // open: en, clr
endmodule

module _6to14 (
  input  [5:0] in_1,
  output [13:0] out_2
);


  assign out_2 = {{8{1'b0}}, in_1};
endmodule

module _6to18 (
  input  [5:0] in_1,
  output [17:0] out_2
);


  assign out_2 = {{13{in_1[5]}}, in_1[4:0]};
endmodule

module _14bAdder (
  input  [13:0] input2,
  input  [13:0] input1,
  output [13:0] sum,
  output co
);

  wire fulladder_1_co, fulladder_2_co, fulladder_3_co, fulladder_4_co, fulladder_5_co, fulladder_6_co,
       fulladder_7_co, fulladder_8_co, fulladder_9_co, fulladder_10_co, fulladder_11_co, fulladder_12_co,
       halfadder_1_co;

  halfAdder halfadder_1 (.a(input2[0]), .b(input1[0]), .sum(sum[0]), .co(halfadder_1_co));
  fullAdder fulladder_1 (.a(input2[1]), .b(input1[1]), .ci(halfadder_1_co), .sum(sum[1]), .co(fulladder_1_co));
  fullAdder fulladder_2 (.a(input2[2]), .b(input1[2]), .ci(fulladder_1_co), .sum(sum[2]), .co(fulladder_2_co));
  fullAdder fulladder_3 (.a(input2[3]), .b(input1[3]), .ci(fulladder_2_co), .sum(sum[3]), .co(fulladder_3_co));
  fullAdder fulladder_4 (.a(input2[4]), .b(input1[4]), .ci(fulladder_3_co), .sum(sum[4]), .co(fulladder_4_co));
  fullAdder fulladder_5 (.a(input2[5]), .b(input1[5]), .ci(fulladder_4_co), .sum(sum[5]), .co(fulladder_5_co));
  fullAdder fulladder_6 (.a(input2[6]), .b(input1[6]), .ci(fulladder_5_co), .sum(sum[6]), .co(fulladder_6_co));
  fullAdder fulladder_7 (.a(input2[7]), .b(input1[7]), .ci(fulladder_6_co), .sum(sum[7]), .co(fulladder_7_co));
  fullAdder fulladder_8 (.a(input2[8]), .b(input1[8]), .ci(fulladder_7_co), .sum(sum[8]), .co(fulladder_8_co));
  fullAdder fulladder_9 (.a(input2[9]), .b(input1[9]), .ci(fulladder_8_co), .sum(sum[9]), .co(fulladder_9_co));
  fullAdder fulladder_10 (.a(input2[10]), .b(input1[10]), .ci(fulladder_9_co), .sum(sum[10]), .co(fulladder_10_co));
  fullAdder fulladder_11 (.a(input2[11]), .b(input1[11]), .ci(fulladder_10_co), .sum(sum[11]), .co(fulladder_11_co));
  fullAdder fulladder_12 (.a(input2[12]), .b(input1[12]), .ci(fulladder_11_co), .sum(sum[12]), .co(fulladder_12_co));
  fullAdder fulladder_13 (.a(input2[13]), .b(input1[13]), .ci(fulladder_12_co), .sum(sum[13]), .co(co));
endmodule

module PCSelector (
  input  [17:0] input1,
  input  [17:0] input2,
  input  [2:0] BChoise,
  input  Enable,
  output out
);

  wire GE_out, LE_out, multiplexer_1_out, NF, not_1_out, PF, ZF;

  _18bComp u_18bcomp_1 (.input1(input1), .input2(input2), .ZF(ZF), .PF(PF), .NF(NF));
  or GE (GE_out, PF, ZF);
  or LE (LE_out, ZF, NF);
  Multiplexer #(.select(3), .enable("false")) multiplexer_1 (
    .in0(ZF), .in1(PF), .in2(NF), .in3(GE_out), .in4(LE_out), .out(multiplexer_1_out), .sel(BChoise));  // open: in5, in6, in7
  not not_1 (not_1_out, Enable);
  assign out = not_1_out ? 1'b0 : 1'bz;  // Controlled_Buffer controlled_buffer_1
  assign out = Enable ? multiplexer_1_out : 1'bz;  // Controlled_Buffer controlled_buffer_2

  // Other names for the same wires on the sheet: Choise[2:0] = BChoise; enb = Enable
endmodule

module X (
  input  [9:0] in_1,
  input  [17:0] in_2,
  input  in_3,
  input  [17:0] in_4,
  output [17:0] out_5
);

  wire clock_1_out, not_1_out, undriven;
  wire [17:0] ram_1_data, register_1_q;

  Clock clock_1 (.out(clock_1_out));
  RAM #(.addrWidth(10), .dataWidth(18)) ram_1 (
    .addr(in_1), .data(ram_1_data), .sel(1'b1), .clk(clock_1_out), .ld(in_3));  // open: clr
  not not_1 (not_1_out, in_3);
  assign ram_1_data = not_1_out ? in_2 : 18'bz;  // Controlled_Buffer controlled_buffer_1
  assign out_5 = in_3 ? ram_1_data : 18'bz;  // Controlled_Buffer controlled_buffer_2
  Register #(.width(18)) register_1 (.D(in_4), .en(undriven), .Q(register_1_q), .clk(undriven));  // open: clr

  // Other names for the same wires on the sheet: Z = in_3
endmodule
